// Logisim project PROM.circ as structural Verilog: 1 circuit, main circuit main
module main (
  input  A0,
  input  A1,
  input  A2,
  input  A3,
  input  A4,
  input  A8,
  input  A5,
  input  A6,
  input  A7,
  input  T6,
  input  A15,
  input  A14,
  input  A13,
  input  A12,
  input  A11,
  input  A10,
  input  A9
);

  wire and_1_out, and_2_out, and_3_out, and_4_out, and_5_out, and_6_out, and_7_out, and_8_out, nand_1_out,
       nand_2_out, nor_1_out, nor_2_out, not_1_out, not_2_out, pull_resistor_1_node, pull_resistor_2_node;
  wire [3:0] nand_6_out, nand_10_out;
  wire [7:0] rom_1_data;

  Pull_Resistor #(.pull(1)) pull_resistor_1 (.node(pull_resistor_1_node));
  Pull_Resistor #(.pull(1)) pull_resistor_2 (.node(pull_resistor_2_node));
  and and_1 (and_1_out, A15, pull_resistor_1_node);
  and and_2 (and_2_out, A14, pull_resistor_1_node);
  and and_3 (and_3_out, A13, pull_resistor_1_node);
  and and_4 (and_4_out, A12, pull_resistor_1_node);
  and and_5 (and_5_out, 1'b0, pull_resistor_2_node);
  and and_6 (and_6_out, A11, pull_resistor_2_node);
  and and_7 (and_7_out, A10, pull_resistor_2_node);
  and and_8 (and_8_out, 1'b0, pull_resistor_2_node);
  nor nor_1 (nor_1_out, and_1_out, and_2_out, and_3_out, and_4_out);
  not not_1 (not_1_out, T6);
  nor nor_2 (nor_2_out, and_5_out, and_6_out, and_7_out, and_8_out);
  Hex_Digit_Display hex_digit_display_1 (.value({A15, A14, A13, A12}));  // open: dp
  LED ROM_EN (.in(nand_1_out));
  nand nand_1 (nand_1_out, not_1_out, nor_1_out, nor_2_out, A9);
  Hex_Digit_Display hex_digit_display_2 (.value({A11, A10, A9, A8}));  // open: dp
  Hex_Digit_Display hex_digit_display_3 (.value({A7, A6, A5, A4}));  // open: dp
  ROM #(.addrWidth(9)) rom_1 (.addr({A7, A6, A5, A8, A4, A3, A2, A1, A0}), .data(rom_1_data));
  not not_2 (not_2_out, nand_1_out);
  nand nand_2 (nand_2_out, not_2_out, not_2_out);
  LED T8 (.in(nand_2_out));
  Hex_Digit_Display hex_digit_display_4 (.value({A3, A2, A1, A0}));  // open: dp
  nand nand_3 (nand_6_out[3], not_2_out, rom_1_data[7]);
  nand nand_4 (nand_6_out[2], not_2_out, rom_1_data[6]);
  LED D7 (.in(nand_6_out[3]));
  LED D6 (.in(nand_6_out[2]));
  nand nand_5 (nand_6_out[1], not_2_out, rom_1_data[5]);
  nand nand_6 (nand_6_out[0], not_2_out, rom_1_data[4]);
  LED D5 (.in(nand_6_out[1]));
  LED D4 (.in(nand_6_out[0]));
  nand nand_7 (nand_10_out[3], not_2_out, rom_1_data[3]);
  nand nand_8 (nand_10_out[2], not_2_out, rom_1_data[2]);
  LED D3 (.in(nand_10_out[3]));
  LED D2 (.in(nand_10_out[2]));
  nand nand_9 (nand_10_out[1], not_2_out, rom_1_data[1]);
  nand nand_10 (nand_10_out[0], not_2_out, rom_1_data[0]);
  LED D1 (.in(nand_10_out[1]));
  LED D0 (.in(nand_10_out[0]));
  Hex_Digit_Display hex_digit_display_5 (.value(nand_6_out));  // open: dp
  Hex_Digit_Display hex_digit_display_6 (.value(nand_10_out));  // open: dp

  // Notes on the sheet:
  //   contents of rom_1 (hex, n*v repeats v):
  //   f5 65 4b d0 c 80 7d 41 d5 be 73 a1 65 9 a1 65 40 55 d0 73 35 40 fa 18 29 40 37 7 4 80 48 a 2f 7b 3 1
  //   71 84 15 44 f1 81 0 1c 7b 2 2f 1f ea 90 0 2f 0 1 90 6 2f 4 2f f2 14 5a 20 0 c0 14 18 49 5 c0 19 16
  //   31 41 11 80 e 19 31 41 9 80 25 16 49 b0 c0 25 14 49 8d c0 2a 14 4d e7 d0 a0 15 5a 0 4 d0 1e 94 3 3b
  //   7b 41 f1 b1 3a af 14 5a 10 0 d0 2d 94 40 f1 a1 ba 18 49 7 c0 4c 79 40 32 a2 6d be 47 93 4c 79 3 b3
  //   41 95 0 8b 0 8c 9 fa 15 4a 9 f8 c1 da 73 9 1 15 8 bf 73 2 73 62 73 9 e6 a4 31 42 df c0 4 16 49 e0 c0
  //   31 43 80 c0 f5 84 fb 11 2c ee 84 ef 73 1 f8 81 3 1 71 3 7b d 7b 8 80 8 f8 a1 45 80 6 2f 34 2f 2 2f
  //   1f ea 90 0 2f 0 1 90 9a 73 f2 a1 9 1 15 41 85 f9 11 2c 2c 0 f2 81 11 73 73 73 85 73 7 0 8a 8d d2 cf
  //   d2 d2 c5 8a 8d 11 2 73 20 7b e e 8 f8 a1 43 80 6 2f 34 2f 2 2f 3b 80 51 0 2f 40 1f 90 e 8 f8 a1 e 8
  //   f8 7b 3 1 71 3 15 45 15 7b 2 2f ff f0 90 0 2f 0 1 90 43 22 7b 2 2f f6 ff 90 a0 2f 6 2f 14 a1 2a e 8
  //   f8 a1 41 80 4e 7b 8 80 81 a5 ff 80 f3 15 49 e c0 28 81 f5 90 1 d0 81 a5 2a 81 a5 2f a2 f5 fb 17 29
  //   30 27 6 0 81 d0 a2 f5 0 83 d0 a2 e5 88 c0 a2 f5 20 32 a2 f5 0 f d0 3d 18 85 80 81 b5 3a 81 a5 83 80
  //   81 a5 31 40 f c0 4 14 a1 85 81 a5 84 80 81 b5 0 81 90 5e 40 1f 90 49 3 c0 7f 18 7f 16 a1 c5 48 16 31
  //   40 50 c0 72 7b 50 15 49 c8 c0 5 14 49 c3 c0 a 14 a2 e5 49 a2 a5 a0 73 9 fb 10 2c df 84 48 f1 a1 41
  //   85 9 f6 84 fa 15 29 1 f8 81 0 f8 a1 41 85 0 fc 71 c6 c0 72 7b 0 bd c4 79 7b 5f 0 10 90 e e 1 f2 a1
  //   8c 80 0 f2 a1 c5 80 1 80 71 3 73 2 1a
endmodule
