// Logisim project WaitState.circ as structural Verilog: 1 circuit, main circuit main
module main (
  input  A12,
  input  A13,
  input  A14,
  input  A15,
  output ROM_Lookup,
  output DATA_Out
);

  wire and_1_out, and_2_out, and_3_out, and_4_out, and_5_out, and_6_out, and_7_out, and_8_out, clock_1_out,
       d_ff_1_q, d_ff_3_q, d_ff_5_q, not_1_out, not_2_out, not_3_out, not_4_out, pull_resistor_1_node;

  Clock clock_1 (.out(clock_1_out));
  not not_1 (not_1_out, A12);
  not not_2 (not_2_out, A13);
  not not_3 (not_3_out, A14);
  and and_1 (and_1_out, clock_1_out, not_1_out);
  and and_2 (and_2_out, and_1_out, and_3_out);
  and and_3 (and_3_out, clock_1_out, not_2_out);
  and and_4 (and_4_out, clock_1_out, not_3_out);
  and and_5 (and_5_out, and_4_out, and_6_out);
  and and_6 (and_6_out, clock_1_out, A15);
  and and_7 (and_7_out, and_2_out, and_5_out);
  and and_8 (and_8_out, and_7_out, not_4_out);
  not not_4 (not_4_out, d_ff_5_q);
  Pull_Resistor #(.pull(1)) pull_resistor_1 (.node(pull_resistor_1_node));
  D_Flip_Flop d_ff_1 (
    .clk(and_8_out), .D(pull_resistor_1_node), .Q(d_ff_1_q), .reset(d_ff_5_q));  // open: Qn, preset, en
  D_Flip_Flop d_ff_2 (.clk(and_8_out), .D(d_ff_1_q), .Q(ROM_Lookup), .reset(d_ff_5_q));  // open: Qn, preset, en
  D_Flip_Flop d_ff_3 (.clk(and_8_out), .D(ROM_Lookup), .Q(d_ff_3_q), .reset(d_ff_5_q));  // open: Qn, preset, en
  D_Flip_Flop d_ff_4 (.clk(and_8_out), .D(d_ff_3_q), .Q(DATA_Out), .reset(d_ff_5_q));  // open: Qn, preset, en
  D_Flip_Flop d_ff_5 (.clk(and_8_out), .D(DATA_Out), .Q(d_ff_5_q), .reset(d_ff_5_q));  // open: Qn, preset, en
endmodule
