// Logisim project AdapterAddrSelect.circ as structural Verilog: 1 circuit, main circuit main
module main (
  input  in_1,
  input  in_2,
  input  in_3,
  input  in_4,
  input  in_5,
  input  in_6,
  input  in_7,
  input  in_8,
  input  in_9,
  output out_10,
  output out_11,
  output out_12,
  output out_13
);

  wire or_1_out, or_2_out, or_3_out, or_5_out, or_6_out, or_8_out, or_9_out;

  or or_1 (or_1_out, in_1, in_3);
  or or_2 (or_2_out, or_1_out, in_5);
  or or_3 (or_3_out, or_2_out, in_7);
  or or_4 (out_10, or_3_out, in_9);
  or or_5 (or_5_out, in_6, in_7);
  or or_6 (or_6_out, in_7, in_6);
  or or_7 (out_11, in_2, or_8_out);
  or or_8 (or_8_out, in_3, or_5_out);
  or or_9 (or_9_out, or_6_out, in_4);
  or or_10 (out_12, or_9_out, in_5);
  or or_11 (out_13, in_8, in_9);
endmodule
