// Logisim project Clocking.circ as structural Verilog: 1 circuit, main circuit main
module main (
  input  A3,
  input  B3,
  input  in_3,
  input  in_4,
  input  in_5,
  input  A2,
  input  in_7,
  input  in_8,
  input  B2,
  input  in_10,
  input  A_B,
  input  in_12,
  input  A_B_2,
  input  in_14,
  input  A_B_3,
  input  in_16,
  input  in_17,
  input  A1,
  input  in_19,
  input  in_20,
  input  B1,
  input  in_22,
  input  in_23,
  input  in_24,
  input  in_25,
  input  A0,
  input  in_27,
  input  B0
);

  wire and_2_out, and_3_out, and_4_out, and_5_out, and_6_out, and_7_out, and_8_out, and_9_out, nand_1_out,
       nand_2_out, nand_3_out, nand_4_out, nand_6_out, nor_1_out, nor_2_out, not_13_out, not_14_out,
       not_15_out, not_16_out, not_17_out, not_18_out, not_19_out, not_20_out, not_21_out, not_22_out,
       not_23_out, not_24_out, not_25_out, not_26_out, not_27_out, not_28_out, not_29_out, not_30_out,
       xnor_1_out, xnor_2_out, xnor_3_out, xnor_4_out, xnor_5_out, xnor_6_out, xnor_7_out, xnor_8_out;

  nand nand_1 (nand_1_out, A3, B3);
  nand nand_2 (nand_2_out, A2, B2);
  nand nand_3 (nand_3_out, A1, B1);
  nand nand_4 (nand_4_out, A0, B0);
  // AND_Gate and_1 has open pins: in0=B3, in1=nand_1_out, out=open
  and and_2 (and_2_out, A3, nand_1_out);
  nor nor_1 (nor_1_out, and_2_out, and_3_out);
  and and_3 (and_3_out, nand_1_out, B3);
  and and_4 (and_4_out, A2, nand_2_out);
  nor nor_2 (nor_2_out, and_4_out, and_5_out);
  and and_5 (and_5_out, nand_2_out, B2);
  and and_6 (and_6_out, A1, nand_3_out);
  // NOR_Gate nor_3 has open pins: in0=and_6_out, in1=and_7_out, out=open
  and and_7 (and_7_out, nand_3_out, B1);
  and and_8 (and_8_out, A0, nand_4_out);
  // NOR_Gate nor_4 has open pins: in0=and_8_out, in1=and_9_out, out=open
  and and_9 (and_9_out, nand_4_out, B0);
  // AND_Gate and_10 has open pins: in0=nand_1_out, in1=A3, out=open
  // AND_Gate and_11 has open pins: in0=B2, in1=nand_2_out, in2=nor_1_out, out=open
  // AND_Gate and_12 has open pins: in0=B1, in1=nand_3_out, in2=nor_1_out, in3=nor_2_out, out=open
  // AND_Gate and_13 has open pins: in0=B0, in1=nand_4_out, in2=nor_1_out, in3=nor_2_out, out=open
  // AND_Gate and_14 is placed but not wired
  // AND_Gate and_15 is placed but not wired
  // AND_Gate and_16 is placed but not wired
  // AND_Gate and_17 is placed but not wired
  // AND_Gate and_18 is placed but not wired
  // AND_Gate and_19 is placed but not wired
  // AND_Gate and_20 is placed but not wired
  // NOT_Gate not_1 is placed but not wired
  // NOT_Gate not_2 is placed but not wired
  // NOT_Gate not_3 is placed but not wired
  // NOT_Gate not_4 is placed but not wired
  // NOT_Gate not_5 is placed but not wired
  // NOT_Gate not_6 is placed but not wired
  // NOT_Gate not_7 is placed but not wired
  // NOT_Gate not_8 is placed but not wired
  // NOT_Gate not_9 is placed but not wired
  // NOT_Gate not_10 is placed but not wired
  // NOT_Gate not_11 is placed but not wired
  // NOT_Gate not_12 is placed but not wired
  // AND_Gate and_21 is placed but not wired
  // AND_Gate and_22 is placed but not wired
  // AND_Gate and_23 is placed but not wired
  // NAND_Gate nand_5 has open pins: in0=not_13_out, in1=not_13_out, in2=nand_6_out, in3=nand_6_out, out=open
  // NOT_Gate not_13 has open pins: in=open, out=not_13_out
  nand nand_6 (nand_6_out, xnor_1_out, xnor_2_out, xnor_3_out, xnor_4_out, xnor_5_out, xnor_6_out, xnor_7_out, xnor_8_out);
  not not_14 (not_14_out, in_3);
  xnor xnor_1 (xnor_1_out, not_14_out, not_15_out);
  not not_15 (not_15_out, in_4);
  not not_16 (not_16_out, in_5);
  xnor xnor_2 (xnor_2_out, not_16_out, not_17_out);
  not not_17 (not_17_out, in_7);
  not not_18 (not_18_out, in_8);
  xnor xnor_3 (xnor_3_out, not_18_out, not_19_out);
  not not_19 (not_19_out, in_10);
  not not_20 (not_20_out, in_12);
  xnor xnor_4 (xnor_4_out, not_20_out, not_21_out);
  not not_21 (not_21_out, in_14);
  not not_22 (not_22_out, in_16);
  xnor xnor_5 (xnor_5_out, not_22_out, not_23_out);
  not not_23 (not_23_out, in_17);
  not not_24 (not_24_out, in_19);
  xnor xnor_6 (xnor_6_out, not_24_out, not_25_out);
  not not_25 (not_25_out, in_20);
  not not_26 (not_26_out, in_22);
  xnor xnor_7 (xnor_7_out, not_26_out, not_27_out);
  not not_27 (not_27_out, in_23);
  not not_28 (not_28_out, in_24);
  xnor xnor_8 (xnor_8_out, not_28_out, not_29_out);
  not not_29 (not_29_out, in_25);
  not not_30 (not_30_out, in_27);
endmodule
