// Logisim project Clocking_1.circ as structural Verilog: 1 circuit, main circuit main
module main (
  input  A12,
  input  A13,
  input  T_24,
  input  A14,
  input  T_25,
  input  A15,
  input  T_23,
  input  A8,
  input  A5,
  input  A6,
  input  A7,
  input  A9,
  input  A10,
  input  A11,
  input  PIN_6,
  input  PIN_7,
  output out_17,
  output out_18
);

  wire and_1_out, C3_pin1, C3_pin6, C3_pin10, C3_pin11, CLK_out, D2_out, d_ff_2_q, d_ff_4_q, d_ff_5_q,
       d_ff_6_q, d_ff_7_q, nand_2_out, nand_3_out, nand_4_out, not_1_out, not_2_out, not_3_out,
       pull_resistor_1_node, xnor_1_out, xnor_2_out, xnor_3_out, xnor_4_out, xnor_5_out, xnor_6_out,
       xnor_7_out, xnor_8_out;

  Pull_Resistor #(.pull(1)) pull_resistor_1 (.node(pull_resistor_1_node));
  D_Flip_Flop d_ff_1 (.D(and_1_out), .clk(CLK_out), .Q(out_17), .reset(not_3_out));  // open: Qn, preset
  and and_1 (and_1_out, nand_2_out, pull_resistor_1_node);
  _7485 #(.ShowInternalStructure("true")) C3 (
    .pin1(C3_pin1), .pin2(C3_pin1), .pin3(pull_resistor_1_node), .pin4(C3_pin1), .pin6(C3_pin6),
    .pin15(T_24), .pin14(C3_pin1), .pin13(T_25), .pin12(T_23), .pin11(C3_pin11), .pin10(C3_pin10),
    .pin9(C3_pin11));  // open: pin5, pin7
  // NAND_Gate nand_1 has open pins: in0=C3_pin6, out=open
  not not_1 (not_1_out, C3_pin6);
  nand nand_2 (nand_2_out, not_1_out, not_1_out, D2_out, D2_out);
  D_Flip_Flop d_ff_2 (.D(out_17), .clk(CLK_out), .Q(d_ff_2_q), .reset(not_3_out));  // open: Qn, preset
  D_Flip_Flop d_ff_3 (.D(d_ff_2_q), .clk(CLK_out), .Q(out_18), .reset(not_3_out));  // open: Qn, preset
  nand D2 (D2_out, xnor_1_out, xnor_2_out, xnor_3_out, xnor_4_out, xnor_5_out, xnor_6_out, xnor_7_out, xnor_8_out, not_2_out);
  D_Flip_Flop d_ff_4 (.D(out_18), .clk(CLK_out), .Q(d_ff_4_q), .reset(not_3_out));  // open: Qn, preset
  xnor xnor_1 (xnor_1_out, ~pull_resistor_1_node, ~1'b1);  // XNOR_Gate
  xnor xnor_2 (xnor_2_out, ~A8, ~1'b1);  // XNOR_Gate
  xnor xnor_3 (xnor_3_out, ~A5, ~1'b0);  // XNOR_Gate
  xnor xnor_4 (xnor_4_out, ~A6, ~1'b0);  // XNOR_Gate
  xnor xnor_5 (xnor_5_out, ~A7, ~1'b0);  // XNOR_Gate
  xnor xnor_6 (xnor_6_out, ~A9, ~1'b0);  // XNOR_Gate
  xnor xnor_7 (xnor_7_out, ~A10, ~1'b0);  // XNOR_Gate
  xnor xnor_8 (xnor_8_out, ~A11, ~1'b0);  // XNOR_Gate
  not not_2 (not_2_out, C3_pin10);
  D_Flip_Flop d_ff_5 (.D(d_ff_4_q), .clk(CLK_out), .Q(d_ff_5_q), .reset(not_3_out));  // open: Qn, preset
  D_Flip_Flop d_ff_6 (.D(d_ff_5_q), .clk(CLK_out), .Q(d_ff_6_q), .reset(not_3_out));  // open: Qn, preset
  nand E1 (C3_pin10, A12, A13, A14, A15);
  D_Flip_Flop d_ff_7 (.D(d_ff_6_q), .clk(CLK_out), .Q(d_ff_7_q), .reset(not_3_out));  // open: Qn, preset
  D_Flip_Flop d_ff_8 (.D(d_ff_7_q), .clk(CLK_out), .reset(not_3_out));  // open: Q, Qn, preset
  not not_3 (not_3_out, nand_4_out);
  nand nand_3 (nand_3_out, out_18, out_18);
  Clock CLK (.out(CLK_out));
  nand nand_4 (nand_4_out, PIN_6, PIN_7);
  LED PIN_8_ASSERTLOW (.in(nand_3_out));
  // also tied to GND on the sheet: C3_pin1
  // also tied to VCC on the sheet: C3_pin11
endmodule
