// Logisim project Clocking_2.circ as structural Verilog: 1 circuit, main circuit main
module main (
  input  A12,
  input  A13,
  input  T_24,
  input  A14,
  input  T_25,
  input  A15,
  input  T_23,
  input  A8,
  input  A5,
  input  A6,
  input  A4,
  input  A7,
  input  A9,
  input  A10,
  input  A11,
  input  T6_RDIN,
  input  T7_WTIN
);

  wire and_1_out, and_2_out, and_3_out, buffer_1_out, buffer_2_out, C3_pin1, C3_pin6, C3_pin10, C3_pin11,
       CLK_out, D2_out, d_ff_1_q, d_ff_2_q, d_ff_3_q, d_ff_4_q, d_ff_5_q, d_ff_6_q, d_ff_7_q, nand_1_out,
       nand_3_out, nand_4_out, nand_5_out, nand_6_out, nand_8_out, nand_11_out, nand_12_out, not_1_out,
       not_2_out, not_3_out, not_4_out, not_5_out, not_6_out, not_7_out, not_8_out, not_9_out, not_10_out,
       pull_resistor_1_node, xnor_1_out, xnor_2_out, xnor_3_out, xnor_4_out, xnor_5_out, xnor_6_out,
       xnor_7_out, xnor_8_out;

  Pull_Resistor #(.pull(1)) pull_resistor_1 (.node(pull_resistor_1_node));
  nand nand_1 (nand_1_out, not_1_out, not_1_out, D2_out, D2_out);
  D_Flip_Flop d_ff_1 (.D(and_1_out), .clk(CLK_out), .Q(d_ff_1_q), .reset(not_3_out));  // open: Qn, preset
  and and_1 (and_1_out, nand_1_out, pull_resistor_1_node);
  _7485 #(.ShowInternalStructure("true")) C3 (
    .pin1(C3_pin1), .pin2(C3_pin1), .pin3(pull_resistor_1_node), .pin4(C3_pin1), .pin6(C3_pin6),
    .pin15(T_24), .pin14(C3_pin1), .pin13(T_25), .pin12(T_23), .pin11(C3_pin11), .pin10(C3_pin10),
    .pin9(C3_pin11));  // open: pin5, pin7
  // NAND_Gate nand_2 has open pins: in0=C3_pin6, out=open
  not not_1 (not_1_out, C3_pin6);
  D_Flip_Flop d_ff_2 (.D(d_ff_1_q), .clk(CLK_out), .Q(d_ff_2_q), .reset(not_3_out));  // open: Qn, preset
  D_Flip_Flop d_ff_3 (.D(d_ff_2_q), .clk(CLK_out), .Q(d_ff_3_q), .reset(not_3_out));  // open: Qn, preset
  nand D2 (D2_out, xnor_1_out, xnor_2_out, xnor_3_out, xnor_4_out, xnor_5_out, xnor_6_out, xnor_7_out, xnor_8_out, not_2_out);
  D_Flip_Flop d_ff_4 (.D(d_ff_3_q), .clk(CLK_out), .Q(d_ff_4_q), .reset(not_3_out));  // open: Qn, preset
  xnor xnor_1 (xnor_1_out, ~pull_resistor_1_node, ~1'b1);  // XNOR_Gate
  xnor xnor_2 (xnor_2_out, ~A8, ~1'b1);  // XNOR_Gate
  xnor xnor_3 (xnor_3_out, ~A5, ~1'b0);  // XNOR_Gate
  xnor xnor_4 (xnor_4_out, ~A6, ~1'b0);  // XNOR_Gate
  xnor xnor_5 (xnor_5_out, ~A7, ~1'b0);  // XNOR_Gate
  xnor xnor_6 (xnor_6_out, ~A9, ~1'b0);  // XNOR_Gate
  xnor xnor_7 (xnor_7_out, ~A10, ~1'b0);  // XNOR_Gate
  xnor xnor_8 (xnor_8_out, ~A11, ~1'b0);  // XNOR_Gate
  not not_2 (not_2_out, C3_pin10);
  D_Flip_Flop d_ff_5 (.D(d_ff_4_q), .clk(CLK_out), .Q(d_ff_5_q), .reset(not_3_out));  // open: Qn, preset
  D_Flip_Flop d_ff_6 (.D(d_ff_5_q), .clk(CLK_out), .Q(d_ff_6_q), .reset(not_3_out));  // open: Qn, preset
  D_Flip_Flop d_ff_7 (.D(d_ff_6_q), .clk(CLK_out), .Q(d_ff_7_q), .reset(not_3_out));  // open: Qn, preset
  nand E1 (C3_pin10, A12, A13, A14, A15);
  D_Flip_Flop d_ff_8 (.D(d_ff_7_q), .clk(CLK_out), .reset(not_3_out));  // open: Q, Qn, preset
  not not_3 (not_3_out, nand_5_out);
  nand nand_3 (nand_3_out, C3_pin6, C3_pin6);
  nand nand_4 (nand_4_out, d_ff_3_q, d_ff_3_q);
  not not_4 (not_4_out, T6_RDIN);
  nand nand_5 (nand_5_out, T6_RDIN, T7_WTIN);
  not not_5 (not_5_out, not_4_out);
  not not_6 (not_6_out, A5);
  not not_7 (not_7_out, A4);
  not not_8 (not_8_out, not_4_out);
  nand nand_6 (nand_6_out, not_8_out, d_ff_1_q, d_ff_3_q);
  and and_2 (and_2_out, ~D2_out, ~not_5_out);  // AND_Gate
  not not_9 (not_9_out, not_6_out);
  buf buffer_1 (buffer_1_out, not_9_out);
  not not_10 (not_10_out, not_7_out);
  buf buffer_2 (buffer_2_out, not_10_out);
  and and_3 (and_3_out, ~D2_out, ~nand_6_out);  // AND_Gate
  // NAND_Gate nand_7 has open pins: in0=not_6_out, in1=not_7_out, in2=and_2_out, out=open
  nand nand_8 (nand_8_out, not_6_out, buffer_2_out, and_2_out);
  LED DIP_STROBE (.in(nand_8_out));
  // NAND_Gate nand_9 has open pins: in0=buffer_1_out, in1=not_7_out, in2=and_2_out, out=open
  // NAND_Gate nand_10 has open pins: in0=buffer_1_out, in1=buffer_2_out, in2=and_2_out, out=open
  nand nand_11 (nand_11_out, not_6_out, not_7_out, and_3_out);
  LED DEC_EN_ACT_LOW (.in(nand_11_out));
  nand nand_12 (nand_12_out, not_6_out, buffer_2_out, and_3_out);
  LED HEX_STROBE (.in(nand_12_out));
  // NAND_Gate nand_13 has open pins: in0=buffer_1_out, in1=not_7_out, in2=and_3_out, out=open
  // NAND_Gate nand_14 has open pins: in0=buffer_1_out, in1=buffer_2_out, in2=and_3_out, out=open
  LED T_11 (.in(nand_3_out));
  LED T8_DRDY_ASSERTLOW (.in(nand_4_out));
  Clock CLK (.out(CLK_out));
  // also tied to GND on the sheet: C3_pin1
  // also tied to VCC on the sheet: C3_pin11
endmodule
