// Logisim project HexDisplayControl.circ as structural Verilog: 1 circuit, main circuit main
module main (
  input  AM25LS2521,
  input  A5,
  input  A4,
  input  T6,
  input  SR1,
  input  SR3
);

  wire and_1_out, and_2_out, buffer_1_out, buffer_2_out, nand_1_out, nand_3_out, nand_6_out, nand_7_out,
       not_1_out, not_2_out, not_3_out, not_4_out, not_5_out, not_6_out, not_7_out;

  not not_1 (not_1_out, T6);
  not not_2 (not_2_out, not_1_out);
  not not_3 (not_3_out, not_1_out);
  not not_4 (not_4_out, A5);
  not not_5 (not_5_out, not_4_out);
  not not_6 (not_6_out, A4);
  not not_7 (not_7_out, not_6_out);
  nand nand_1 (nand_1_out, not_2_out, SR1, SR3);
  and and_1 (and_1_out, ~AM25LS2521, ~not_3_out);  // AND_Gate
  buf buffer_1 (buffer_1_out, not_5_out);
  buf buffer_2 (buffer_2_out, not_7_out);
  and and_2 (and_2_out, ~AM25LS2521, ~nand_1_out);  // AND_Gate
  // NAND_Gate nand_2 has open pins: in0=not_4_out, in1=not_6_out, in2=and_1_out, out=open
  nand nand_3 (nand_3_out, not_4_out, buffer_2_out, and_1_out);
  // NAND_Gate nand_4 has open pins: in0=buffer_1_out, in1=not_6_out, in2=and_1_out, out=open
  // NAND_Gate nand_5 has open pins: in0=buffer_1_out, in1=buffer_2_out, in2=and_1_out, out=open
  nand nand_6 (nand_6_out, not_4_out, not_6_out, and_2_out);
  nand nand_7 (nand_7_out, not_4_out, buffer_2_out, and_2_out);
  // NAND_Gate nand_8 has open pins: in0=buffer_1_out, in1=not_6_out, in2=and_2_out, out=open
  // NAND_Gate nand_9 has open pins: in0=buffer_1_out, in1=buffer_2_out, in2=and_2_out, out=open
  LED DIP_STROBE (.in(nand_3_out));
  LED DEC_EN_ACT_LOW (.in(nand_6_out));
  LED HEX_STROBE (.in(nand_7_out));
endmodule
