// Logisim project LS155.circ as structural Verilog: 1 circuit, main circuit main
module main (
  input  Strobe1IG,
  input  Data1C,
  input  SelectB,
  input  SelectA,
  input  Data2IC,
  input  Strobe2IG
);

  wire and_1_out, and_2_out, buffer_1_out, buffer_2_out, nand_1_out, nand_2_out, nand_3_out, nand_4_out,
       nand_5_out, nand_6_out, nand_7_out, nand_8_out, not_1_out, not_2_out, not_3_out, not_4_out, not_5_out;

  not not_1 (not_1_out, Data1C);
  not not_2 (not_2_out, SelectB);
  not not_3 (not_3_out, SelectA);
  and and_1 (and_1_out, ~Strobe1IG, ~not_1_out);  // AND_Gate
  not not_4 (not_4_out, not_2_out);
  buf buffer_1 (buffer_1_out, not_4_out);
  not not_5 (not_5_out, not_3_out);
  buf buffer_2 (buffer_2_out, not_5_out);
  and and_2 (and_2_out, ~Data2IC, ~Strobe2IG);  // AND_Gate
  nand nand_1 (nand_1_out, not_2_out, not_3_out, and_1_out);
  LED led_1 (.in(nand_1_out));
  nand nand_2 (nand_2_out, not_2_out, buffer_2_out, and_1_out);
  LED led_2 (.in(nand_2_out));
  nand nand_3 (nand_3_out, buffer_1_out, not_3_out, and_1_out);
  LED led_3 (.in(nand_3_out));
  nand nand_4 (nand_4_out, buffer_1_out, buffer_2_out, and_1_out);
  LED led_4 (.in(nand_4_out));
  nand nand_5 (nand_5_out, not_2_out, not_3_out, and_2_out);
  LED led_5 (.in(nand_5_out));
  nand nand_6 (nand_6_out, not_2_out, buffer_2_out, and_2_out);
  LED led_6 (.in(nand_6_out));
  nand nand_7 (nand_7_out, buffer_1_out, not_3_out, and_2_out);
  LED led_7 (.in(nand_7_out));
  nand nand_8 (nand_8_out, buffer_1_out, buffer_2_out, and_2_out);
  LED led_8 (.in(nand_8_out));
endmodule
