// Logisim project WriteControl.circ as structural Verilog: 1 circuit, main circuit main
module main (
  input  T11,
  input  A12,
  input  A13,
  input  A14,
  input  A15,
  input  T7,
  input  T6
);

  wire CLK, d_ff_1_q, j_k_ff_1_qn, nand_1_out, nand_2_out, nand_3_out, nand_4_out, nand_5_out, nand_6_out,
       nor_1_out, nor_2_out, nor_3_out, not_1_out, not_2_out, not_3_out, not_5_out, not_6_out, not_7_out,
       not_8_out, P36_CLK_out;

  Clock P36_CLK (.out(P36_CLK_out));
  not not_1 (not_1_out, P36_CLK_out);
  not not_2 (not_2_out, not_3_out);
  not not_3 (not_3_out, not_7_out);
  not not_4 (CLK, not_2_out);
  nor nor_1 (nor_1_out, A12, A13);
  nor nor_2 (nor_2_out, A14, A15);
  not not_5 (not_5_out, not_1_out);
  not not_6 (not_6_out, not_5_out);
  not not_7 (not_7_out, not_6_out);
  nand nand_1 (nand_1_out, nor_1_out, nor_2_out);
  nand nand_2 (nand_2_out, T11, nand_1_out);
  not not_8 (not_8_out, nand_2_out);
  not nand_3 (nand_3_out, nand_1_out);  // NAND_Gate
  J_K_Flip_Flop j_k_ff_1 (.clk(CLK), .Qn(j_k_ff_1_qn));  // open: J, K, Q, preset, reset
  nor nor_3 (nor_3_out, nand_3_out, T7);
  // NOR_Gate nor_4 has open pins: in0=nand_3_out, in1=T6, out=open
  D_Flip_Flop d_ff_1 (.D(nor_3_out), .clk(CLK), .Q(d_ff_1_q));  // open: Qn, preset, reset
  not nand_4 (nand_4_out, not_8_out);  // NAND_Gate
  nand nand_5 (nand_5_out, j_k_ff_1_qn, not_8_out);
  nand nand_6 (nand_6_out, not_8_out, d_ff_1_q);
  nand nand_7 (nand_6_out, not_8_out, d_ff_1_q);
  nand nand_8 (nand_6_out, not_8_out, d_ff_1_q);
  nand nand_9 (nand_6_out, not_8_out, d_ff_1_q);
  // NAND_Gate nand_10 has open pins: in0=not_8_out, out=open
  LED DBUS_DDIS (.in(nand_4_out));
  LED T8 (.in(nand_5_out));
  LED WRITE_ACTIVE_LOW (.in(nand_6_out));
endmodule
