// Logisim project Control.circ as structural Verilog: 1 circuit, main circuit main
module main (
  input  T6,
  input  T7,
  input  A4,
  input  A5,
  input  A6,
  input  A7,
  input  A8,
  input  A9,
  input  A10,
  input  A11,
  input  A12,
  input  A13,
  input  A14,
  input  A0,
  input  A15,
  input  A1,
  input  A2,
  input  A3
);

  wire and_1_out, and_2_out, and_3_out, and_4_out, and_5_out, and_6_out, and_7_out, and_8_out, and_9_out,
       and_10_out, demultiplexer_1_out0, demultiplexer_1_out1, demultiplexer_1_out2, demultiplexer_1_out3,
       demultiplexer_1_out4, demultiplexer_1_out5, demultiplexer_1_out6, demultiplexer_1_out7,
       demultiplexer_1_out8, demultiplexer_1_out9, demultiplexer_1_out10, demultiplexer_1_out11,
       demultiplexer_1_out12, demultiplexer_1_out13, demultiplexer_1_out14, demultiplexer_1_out15,
       nand_1_out, nand_2_out, nand_3_out, nand_4_out, nand_5_out, nand_6_out, nand_7_out, nor_1_out,
       nor_2_out, not_1_out, not_2_out, not_3_out, not_4_out, not_5_out, not_6_out, not_7_out, not_8_out,
       not_9_out, not_25_out, not_26_out, not_27_out, not_28_out, pull_resistor_1_node, pull_resistor_2_node;

  not not_1 (not_1_out, T6);
  not not_2 (not_2_out, T7);
  Pull_Resistor #(.pull(1)) pull_resistor_1 (.node(pull_resistor_1_node));
  not not_3 (not_3_out, not_1_out);
  not not_4 (not_4_out, not_2_out);
  not not_5 (not_5_out, A5);
  not not_6 (not_6_out, A6);
  not not_7 (not_7_out, A7);
  and and_1 (and_1_out, A12, pull_resistor_1_node);
  and and_2 (and_2_out, A13, pull_resistor_1_node);
  and and_3 (and_3_out, A14, pull_resistor_1_node);
  and and_4 (and_4_out, A15, pull_resistor_1_node);
  nand nand_1 (nand_1_out, not_4_out, not_3_out);
  not not_8 (not_8_out, nand_2_out);
  nand nand_2 (nand_2_out, A4, not_5_out, not_6_out, not_7_out, A8, A9, A10, A11);
  nor nor_1 (nor_1_out, and_1_out, and_2_out, and_3_out, and_4_out);
  nand nand_3 (nand_3_out, not_8_out, nor_1_out);
  nand nand_4 (nand_4_out, nand_1_out, not_8_out, nor_1_out);
  not not_9 (not_9_out, nand_4_out);
  Demultiplexer #(.enable("false"), .select(4)) demultiplexer_1 (
    .out0(demultiplexer_1_out0), .out1(demultiplexer_1_out1), .out2(demultiplexer_1_out2),
    .out3(demultiplexer_1_out3), .out4(demultiplexer_1_out4), .out5(demultiplexer_1_out5),
    .out6(demultiplexer_1_out6), .out7(demultiplexer_1_out7), .out8(demultiplexer_1_out8),
    .out9(demultiplexer_1_out9), .out10(demultiplexer_1_out10), .out11(demultiplexer_1_out11),
    .out12(demultiplexer_1_out12), .out13(demultiplexer_1_out13), .out14(demultiplexer_1_out14),
    .out15(demultiplexer_1_out15), .in(not_9_out), .sel({A3, A2, A1, A0}));
  // NOT_Gate not_10 has open pins: in=demultiplexer_1_out0, out=open
  // NOT_Gate not_11 has open pins: in=demultiplexer_1_out1, out=open
  // NOT_Gate not_12 has open pins: in=demultiplexer_1_out2, out=open
  // NOT_Gate not_13 has open pins: in=demultiplexer_1_out3, out=open
  // NOT_Gate not_14 has open pins: in=demultiplexer_1_out4, out=open
  // NOT_Gate not_15 has open pins: in=demultiplexer_1_out5, out=open
  // NOT_Gate not_16 has open pins: in=demultiplexer_1_out6, out=open
  // NOT_Gate not_17 has open pins: in=demultiplexer_1_out7, out=open
  // NOT_Gate not_18 has open pins: in=demultiplexer_1_out8, out=open
  // NOT_Gate not_19 has open pins: in=demultiplexer_1_out9, out=open
  // NOT_Gate not_20 has open pins: in=demultiplexer_1_out10, out=open
  // NOT_Gate not_21 has open pins: in=demultiplexer_1_out11, out=open
  // NOT_Gate not_22 has open pins: in=demultiplexer_1_out12, out=open
  // NOT_Gate not_23 has open pins: in=demultiplexer_1_out13, out=open
  // NOT_Gate not_24 has open pins: in=demultiplexer_1_out14, out=open
  not not_25 (not_25_out, demultiplexer_1_out15);
  not not_26 (not_26_out, nand_4_out);
  and and_5 (and_5_out, not_4_out, pull_resistor_2_node);
  and and_6 (and_6_out, not_4_out, pull_resistor_2_node);
  and and_7 (and_7_out, nand_3_out, pull_resistor_2_node);
  and and_8 (and_8_out, nand_3_out, pull_resistor_2_node);
  Pull_Resistor #(.pull(1)) pull_resistor_2 (.node(pull_resistor_2_node));
  nand nand_5 (nand_5_out, not_26_out, not_26_out);
  LED T11 (.in(nand_5_out));
  nand nand_6 (nand_6_out, not_26_out, not_26_out);
  LED T8 (.in(nand_6_out));
  nor nor_2 (nor_2_out, and_5_out, and_6_out, and_7_out, and_8_out);
  not nand_7 (nand_7_out, nor_2_out);  // NAND_Gate
  not not_27 (not_27_out, nand_7_out);
  and and_9 (and_9_out, nor_2_out, not_28_out);
  not not_28 (not_28_out, not_25_out);
  and and_10 (and_10_out, not_27_out, and_9_out);
  LED CLK_CIH (.in(and_10_out));
endmodule
