// Logisim project Interrupts.circ as structural Verilog: 1 circuit, main circuit main
module main (
  input  B33,
  input  in_2,
  input  in_3,
  input  in_4,
  input  in_5,
  input  in_6,
  input  A_B,
  input  T29,
  input  RESET,
  input  Y0,
  output T33,
  output T13,
  output T14,
  output T27,
  output T15,
  output T16
);

  wire and_1_out, and_2_out, and_3_out, and_4_out, and_5_out, and_6_out, d_ff_1_qn, j_k_ff_1_q, nand_1_out,
       nand_2_out, nand_3_out, nand_5_out, nand_7_out, nand_8_out, not_1_out, not_2_out, not_3_out,
       not_4_out, not_5_out, pull_resistor_1_node;

  not not_1 (not_1_out, and_6_out);
  not not_2 (not_2_out, B33);
  J_K_Flip_Flop j_k_ff_1 (.J(in_2), .clk(in_3), .K(in_4), .Q(j_k_ff_1_q));  // open: Qn, preset, en, reset
  D_Flip_Flop d_ff_1 (.clk(in_5), .D(in_6), .Qn(d_ff_1_qn), .preset(not_1_out));  // open: Q, en, reset
  not not_3 (not_3_out, T29);
  and and_1 (and_1_out, j_k_ff_1_q, d_ff_1_qn);
  not not_4 (not_4_out, not_3_out);
  and and_2 (and_2_out, not_2_out, and_1_out);
  nand nand_1 (nand_1_out, and_1_out, A_B, not_2_out, not_4_out);
  nand nand_2 (nand_2_out, nand_8_out, and_2_out);
  nand nand_3 (nand_3_out, and_2_out, nand_5_out);
  and and_3 (and_3_out, nand_5_out, not_3_out);
  nand nand_4 (T33, not_2_out, nand_3_out);
  nand nand_5 (nand_5_out, nand_3_out, nand_1_out);
  nand nand_6 (T27, nand_5_out, A_B);
  nand nand_7 (nand_7_out, nand_5_out, not_3_out);
  nand nand_8 (nand_8_out, nand_7_out, nand_2_out);
  not not_5 (not_5_out, and_4_out);
  and and_4 (and_4_out, nand_8_out, not_4_out);
  and and_5 (and_5_out, RESET, Y0);
  Pull_Resistor #(.pull(1)) pull_resistor_1 (.node(pull_resistor_1_node));
  and and_6 (and_6_out, not_5_out, and_5_out);
  nand nand_9 (T13, 1'b0, and_3_out);
  nand nand_10 (T14, and_3_out, 1'b0);
  nand nand_11 (T15, 1'b0, and_3_out);
  nand nand_12 (T16, and_3_out, pull_resistor_1_node);
endmodule
