// Logisim project Interrupts_LE.circ as structural Verilog: 1 circuit, main circuit main
module main (
  input  B33,
  input  in_2,
  input  in_3,
  input  in_4,
  input  in_5,
  input  in_6,
  input  T29,
  input  RESET,
  input  T21,
  input  Y0,
  input  T20,
  input  T19,
  input  T18
);

  wire and_1_out, and_2_out, and_3_out, and_4_out, and_5_out, and_6_out, d_ff_1_qn, j_k_ff_1_q, n7485_1_pin1,
       n7485_1_pin7, n7485_1_pin9, n7485_1_pin10, n7485_1_pin12, n7485_1_pin13, n7485_1_pin15, nand_1_out,
       nand_2_out, nand_3_out, nand_4_out, nand_5_out, nand_6_out, nand_7_out, nand_8_out, nand_9_out,
       nand_10_out, nand_11_out, nand_12_out, not_1_out, not_2_out, not_3_out, not_4_out, not_5_out,
       pull_resistor_1_node;

  J_K_Flip_Flop j_k_ff_1 (.J(in_2), .K(in_3), .clk(in_4), .Q(j_k_ff_1_q));  // open: Qn, preset, reset
  D_Flip_Flop d_ff_1 (.D(in_5), .clk(in_6), .Qn(d_ff_1_qn), .preset(not_1_out));  // open: Q, reset
  not not_1 (not_1_out, and_6_out);
  not not_2 (not_2_out, B33);
  not not_3 (not_3_out, T29);
  and and_1 (and_1_out, j_k_ff_1_q, d_ff_1_qn);
  not not_4 (not_4_out, not_3_out);
  and and_2 (and_2_out, not_2_out, and_1_out);
  nand nand_1 (nand_1_out, and_1_out, n7485_1_pin7, not_2_out, not_4_out);
  nand nand_2 (nand_2_out, nand_8_out, and_2_out);
  nand nand_3 (nand_3_out, and_2_out, nand_5_out);
  and and_3 (and_3_out, nand_5_out, not_3_out);
  nand nand_4 (nand_4_out, not_2_out, nand_3_out);
  nand nand_5 (nand_5_out, nand_3_out, nand_1_out);
  nand nand_6 (nand_6_out, nand_5_out, n7485_1_pin7);
  nand nand_7 (nand_7_out, nand_5_out, not_3_out);
  nand nand_8 (nand_8_out, nand_7_out, nand_2_out);
  LED T33 (.in(nand_4_out));
  LED T27 (.in(nand_6_out));
  and and_4 (and_4_out, nand_8_out, not_4_out);
  not not_5 (not_5_out, and_4_out);
  and and_5 (and_5_out, RESET, Y0);
  Pull_Resistor #(.pull(1)) pull_resistor_1 (.node(pull_resistor_1_node));
  _7485 #(.ShowInternalStructure("true")) u_7485_1 (
    .pin1(n7485_1_pin1), .pin7(n7485_1_pin7), .pin15(n7485_1_pin15), .pin14(n7485_1_pin1),
    .pin13(n7485_1_pin13), .pin12(n7485_1_pin12), .pin11(n7485_1_pin1), .pin10(n7485_1_pin10),
    .pin9(n7485_1_pin9));  // open: pin2, pin3, pin4, pin5, pin6
  and and_6 (and_6_out, not_5_out, and_5_out);
  nand nand_9 (nand_9_out, 1'b0, and_3_out);
  nand nand_10 (nand_10_out, and_3_out, 1'b0);
  nand nand_11 (nand_11_out, 1'b0, and_3_out);
  nand nand_12 (nand_12_out, and_3_out, pull_resistor_1_node);
  Pull_Resistor #(.pull(1)) pull_resistor_2 (.node(n7485_1_pin9));
  LED T13 (.in(nand_9_out));
  LED T14 (.in(nand_10_out));
  LED T15 (.in(nand_11_out));
  LED T16 (.in(nand_12_out));
  not not_6 (n7485_1_pin15, T21);
  not not_7 (n7485_1_pin13, T20);
  not not_8 (n7485_1_pin12, T19);
  not not_9 (n7485_1_pin10, T18);
  // also tied to GND on the sheet: n7485_1_pin1
endmodule
