// Logisim project F20F.circ as structural Verilog: 1 circuit, main circuit main
module main (
  input  F20F_RQ,
  input  Port_CLK,
  input  Port_SEL,
  input  R_T_CLK,
  input  R_T_SEL,
  output nD7_Card,
  output nD6_Card,
  output nD5_Card,
  output nD4_Card,
  output D3_Unasserted,
  output nD2_MUX,
  output nD1_MUX,
  output D0_Rx_Tx
);

  wire d_ff_1_q, d_ff_2_q, nand_1_out, nand_2_out, nand_3_out, nand_4_out, nand_5_out, nand_6_out;

  D_Flip_Flop d_ff_1 (.clk(Port_CLK), .D(Port_SEL), .Q(d_ff_1_q));  // open: Qn, preset, en, reset
  D_Flip_Flop d_ff_2 (.clk(R_T_CLK), .D(R_T_SEL), .Q(d_ff_2_q));  // open: Qn, preset, en, reset
  nand nand_1 (nand_1_out, 1'b1, F20F_RQ);
  nand nand_2 (nand_2_out, 1'b1, F20F_RQ);
  nand nand_3 (nand_3_out, 1'b1, F20F_RQ);
  nand nand_4 (nand_4_out, 1'b1, F20F_RQ);
  nand nand_5 (nand_5_out, d_ff_1_q, F20F_RQ);
  nand nand_6 (nand_6_out, d_ff_2_q, F20F_RQ);
  not not_1 (nD7_Card, nand_1_out);
  not not_2 (nD6_Card, nand_2_out);
  not not_3 (nD5_Card, nand_3_out);
  not not_4 (nD4_Card, nand_4_out);
  not not_5 (nD1_MUX, nand_5_out);
  not not_6 (D0_Rx_Tx, nand_6_out);

  // Notes on the sheet:
  //   F20F = 1111 0 00/01 0/1
  //   F20F = Card No. (4-bits), 0, MUX# (2-bits), R/T (1-bit)
  //   Open Collector NANDs
endmodule
