// Logisim project INT_1.circ as structural Verilog: 1 circuit, main circuit main
module main (
  input  INTIN,
  input  INTACK,
  input  CPL0,
  input  CPL1,
  input  CPL2,
  input  CPL3,
  input  MUX_IRQ,
  input  _0xF20F,
  output INR0,
  output INR1,
  output INR2,
  output INR3,
  output INTOUT,
  output INTRQ,
  output F20F_RQ
);

  wire adder_1_cout, d_ff_2_q, nand_1_out, nand_2_out, nand_3_out, nand_4_out, nand_6_out, nand_7_out,
       nand_8_out, nand_9_out, nand_10_out, nand_11_out, nor_1_out, nor_2_out, not_1_out, not_6_out,
       not_7_out, not_8_out, not_9_out, or_1_out;
  wire [2:2] d_ff_1_q;
  wire [3:0] not_2_out;

  not not_1 (not_1_out, INTACK);
  not not_2 (not_2_out[0], CPL0);
  not not_3 (not_2_out[1], CPL1);
  not not_4 (not_2_out[2], CPL2);
  not not_5 (not_2_out[3], CPL3);
  D_Flip_Flop d_ff_1 (.clk(MUX_IRQ), .D(1'b1), .Q(d_ff_1_q[2]), .reset(_0xF20F));  // open: Qn, preset, en
  not not_6 (not_6_out, INTIN);
  not not_7 (not_7_out, not_1_out);
  not not_8 (not_8_out, not_7_out);
  Adder #(.width(4)) adder_1 (
    .a(not_2_out), .b({1'b0, {2{d_ff_1_q[2]}}, 1'b0}), .cout(adder_1_cout));  // open: out, cin
  not not_9 (not_9_out, adder_1_cout);
  nand nand_1 (nand_1_out, not_9_out, not_8_out);
  or or_1 (or_1_out, not_8_out, d_ff_1_q[2]);
  nand nand_2 (nand_2_out, nand_1_out, not_6_out, nand_3_out);
  nand nand_3 (nand_3_out, nand_2_out, nand_4_out);
  nand nand_4 (nand_4_out, not_6_out, adder_1_cout, or_1_out);
  nor nor_1 (nor_1_out, MUX_IRQ, _0xF20F);
  nor nor_2 (nor_2_out, not_8_out, nand_2_out);
  nand nand_5 (INTOUT, not_6_out, nand_2_out);
  nand nand_6 (nand_6_out, nand_3_out, nand_3_out);
  D_Flip_Flop d_ff_2 (.clk(nor_1_out), .D(nand_3_out), .Q(d_ff_2_q));  // open: Qn, preset, en, reset
  nand nand_7 (nand_7_out, 1'b0, nor_2_out);
  nand nand_8 (nand_8_out, 1'b1, nor_2_out);
  nand nand_9 (nand_9_out, 1'b1, nor_2_out);
  nand nand_10 (nand_10_out, 1'b0, nor_2_out);
  nand nand_11 (nand_11_out, d_ff_2_q, _0xF20F);
  not not_10 (INR0, nand_7_out);
  not not_11 (INR1, nand_8_out);
  not not_12 (INR2, nand_9_out);
  not not_13 (INR3, nand_10_out);
  not not_14 (INTRQ, nand_6_out);
  not not_15 (F20F_RQ, nand_11_out);

  // Notes on the sheet:
  //   Inverters connected to inputs/outputs indicate negative logic
  //   Open Collector NANDs Here
endmodule
